// Logisim project 7_segment.circ as structural Verilog: 2 circuits, main circuit main
module main (
  input  in_1,
  input  in_2,
  input  in_3,
  input  in_4,
  input  in_5,
  input  in_6,
  input  in_7,
  input  in_8,
  input  in_9,
  input  in_10,
  input  in_11,
  input  in_12,
  input  in_13,
  input  in_14,
  input  in_15,
  input  in_16
);

  wire _1_out, _2_out, _4_out, _8_out, b2d_1_p5, b2d_1_p6, b2d_1_p7, b2d_1_p8, b2d_1_p9, b2d_1_p10, b2d_2_p5,
       b2d_2_p6, b2d_2_p7, b2d_2_p8, b2d_2_p9, b2d_2_p10, b2d_3_p5, b2d_3_p6, b2d_3_p7, b2d_3_p8, b2d_3_p9,
       b2d_3_p10, b2d_4_p5, b2d_4_p6, b2d_4_p7, b2d_4_p8, b2d_4_p9, b2d_4_p10, b2d_5_p5, b2d_5_p6, b2d_5_p7,
       b2d_5_p8, b2d_5_p9, b2d_5_p10, undriven, undriven_2, undriven_3, undriven_4, undriven_5;

  // b2d b2d_1: pin names not known; wires that end beside it: in_7, in_9, in_11, in_14, b2d_1_p5, b2d_1_p6, b2d_1_p7, b2d_1_p8, b2d_1_p9, b2d_1_p10
  Button _8 (.out(_8_out));
  Button _4 (.out(_4_out));
  Button _2 (.out(_2_out));
  Button _1 (.out(_1_out));
  // b2d b2d_2: pin names not known; wires that end beside it: in_5, in_6, in_8, in_10, b2d_2_p5, b2d_2_p6, b2d_2_p7, b2d_2_p8, b2d_2_p9, b2d_2_p10
  // b2d b2d_3: pin names not known; wires that end beside it: in_12, in_13, in_15, in_16, b2d_3_p5, b2d_3_p6, b2d_3_p7, b2d_3_p8, b2d_3_p9, b2d_3_p10
  // b2d b2d_4: pin names not known; wires that end beside it: _8_out, _4_out, _2_out, _1_out, b2d_4_p5, b2d_4_p6, b2d_4_p7, b2d_4_p8, b2d_4_p9, b2d_4_p10
  _7_Segment_Display u_7_segment_display_1 (
    .g(undriven_4), .f(b2d_4_p10), .a(b2d_4_p5), .b(b2d_4_p6), .e(b2d_4_p9), .d(b2d_4_p8), .c(b2d_4_p7));  // open: dp
  // b2d b2d_5: pin names not known; wires that end beside it: in_1, in_2, in_3, in_4, b2d_5_p5, b2d_5_p6, b2d_5_p7, b2d_5_p8, b2d_5_p9, b2d_5_p10
  _7_Segment_Display u_7_segment_display_2 (
    .g(undriven), .f(b2d_1_p10), .a(b2d_1_p5), .b(b2d_1_p6), .e(b2d_1_p9), .d(b2d_1_p8), .c(b2d_1_p7));  // open: dp
  _7_Segment_Display u_7_segment_display_3 (
    .g(undriven_3), .f(b2d_3_p10), .a(b2d_3_p5), .b(b2d_3_p6), .e(b2d_3_p9), .d(b2d_3_p8), .c(b2d_3_p7));  // open: dp
  _7_Segment_Display u_7_segment_display_4 (
    .g(undriven_2), .f(b2d_2_p10), .a(b2d_2_p5), .b(b2d_2_p6), .e(b2d_2_p9), .d(b2d_2_p8), .c(b2d_2_p7));  // open: dp
  _7_Segment_Display u_7_segment_display_5 (
    .g(undriven_5), .f(b2d_5_p10), .a(b2d_5_p5), .b(b2d_5_p6), .e(b2d_5_p9), .d(b2d_5_p8), .c(b2d_5_p7));  // open: dp
endmodule

module b2d (
  input  D,
  input  C,
  input  B,
  input  A,
  output [6:0] out_5
);

  wire and_1_out, and_2_out, and_3_out, and_4_out, and_5_out, and_6_out, and_7_out, and_8_out, and_9_out,
       and_10_out, and_11_out, and_12_out, and_13_out, and_14_out, and_15_out, and_16_out, not_1_out,
       not_2_out, not_3_out, not_4_out, not_5_out, not_6_out, not_7_out, not_8_out, not_9_out, not_10_out,
       not_11_out, not_12_out, not_13_out, not_14_out, not_15_out, not_16_out, not_17_out, not_18_out,
       not_19_out, not_20_out, not_21_out;

  not not_1 (not_1_out, C);
  and and_1 (and_1_out, not_1_out, not_2_out);
  not not_2 (not_2_out, A);
  and and_2 (and_2_out, C, A);
  not not_3 (not_3_out, C);
  not not_4 (not_4_out, B);
  and and_3 (and_3_out, not_4_out, not_5_out);
  not not_5 (not_5_out, A);
  and and_4 (and_4_out, B, A);
  not not_6 (not_6_out, B);
  or or_1 (out_5[2], not_6_out, A, C);
  not not_7 (not_7_out, C);
  and and_5 (and_5_out, not_7_out, not_8_out);
  not not_8 (not_8_out, A);
  not not_9 (not_9_out, C);
  and and_6 (and_6_out, not_9_out, B);
  and and_7 (and_7_out, B, not_10_out);
  not not_10 (not_10_out, A);
  and and_8 (and_8_out, C, not_11_out, A);
  not not_11 (not_11_out, B);
  not not_12 (not_12_out, C);
  and and_9 (and_9_out, not_12_out, not_13_out);
  not not_13 (not_13_out, A);
  and and_10 (and_10_out, B, not_14_out);
  not not_14 (not_14_out, A);
  not not_15 (not_15_out, B);
  and and_11 (and_11_out, not_15_out, not_16_out);
  not not_16 (not_16_out, A);
  and and_12 (and_12_out, C, not_17_out);
  not not_17 (not_17_out, B);
  and and_13 (and_13_out, C, not_18_out);
  not not_18 (not_18_out, A);
  not not_19 (not_19_out, C);
  and and_14 (and_14_out, not_19_out, B);
  and and_15 (and_15_out, C, not_20_out);
  not not_20 (not_20_out, B);
  and and_16 (and_16_out, C, not_21_out);
  not not_21 (not_21_out, A);
  or or_2 (out_5[0], and_1_out, B, and_2_out, D);
  or or_3 (out_5[1], not_3_out, and_3_out, and_4_out);
  or or_4 (out_5[3], and_5_out, and_6_out, and_7_out, and_8_out, D);
  or or_5 (out_5[4], and_9_out, and_10_out);
  or or_6 (out_5[5], and_11_out, and_12_out, and_13_out, D);
  or or_7 (out_5[6], and_14_out, and_15_out, and_16_out, D);
endmodule
