// Logisim project adding_choose.circ as structural Verilog: 1 circuit, main circuit main
module main (
  input  [15:0] in_1,
  input  [15:0] in_2,
  input  in_3,
  output [15:0] out_4
);

  wire [15:0] main_1_p3;

  // dodawanie_main main_1: pin names not known; wires that end beside it: in_1, in_2, main_1_p3
  Multiplexer #(.width(16), .enable("false")) multiplexer_1 (
    .in0({16{1'b0}}), .in1(main_1_p3), .out(out_4), .sel(in_3));
  // Probe on out_4
endmodule
