// Logisim project converter_b2d.circ as structural Verilog: 1 circuit, main circuit przetwornik
module przetwornik (
  input  D,
  input  C,
  input  B,
  input  A,
  output [6:0] out_5
);

  wire and_1_out, and_2_out, and_3_out, and_4_out, and_5_out, and_6_out, and_7_out, and_8_out, and_9_out,
       and_10_out, and_11_out, and_12_out, and_13_out, and_14_out, and_15_out, and_16_out, and_17_out,
       not_1_out, not_2_out, not_3_out, not_4_out, not_5_out, not_6_out, not_7_out, not_8_out, not_9_out,
       not_10_out, not_11_out, not_12_out, not_13_out, not_14_out, not_15_out, not_16_out, not_17_out,
       not_18_out, not_19_out, not_20_out, not_21_out, not_22_out;

  not not_1 (not_1_out, C);
  and and_1 (and_1_out, not_1_out, not_2_out);
  not not_2 (not_2_out, A);
  not not_3 (not_3_out, C);
  and and_2 (and_2_out, not_3_out, B);
  and and_3 (and_3_out, C, A);
  not not_4 (not_4_out, C);
  not not_5 (not_5_out, B);
  and and_4 (and_4_out, not_5_out, not_6_out);
  not not_6 (not_6_out, A);
  and and_5 (and_5_out, B, A);
  not not_7 (not_7_out, B);
  or or_1 (out_5[4], not_7_out, A, C);
  not not_8 (not_8_out, C);
  and and_6 (and_6_out, not_8_out, not_9_out);
  not not_9 (not_9_out, A);
  not not_10 (not_10_out, C);
  and and_7 (and_7_out, not_10_out, B);
  and and_8 (and_8_out, B, not_11_out);
  not not_11 (not_11_out, A);
  not not_12 (not_12_out, B);
  and and_9 (and_9_out, C, not_12_out, A);
  not not_13 (not_13_out, C);
  and and_10 (and_10_out, not_13_out, not_14_out);
  not not_14 (not_14_out, A);
  and and_11 (and_11_out, B, not_15_out);
  not not_15 (not_15_out, A);
  not not_16 (not_16_out, B);
  and and_12 (and_12_out, not_16_out, not_17_out);
  not not_17 (not_17_out, A);
  and and_13 (and_13_out, C, not_18_out);
  not not_18 (not_18_out, B);
  and and_14 (and_14_out, C, not_19_out);
  not not_19 (not_19_out, A);
  not not_20 (not_20_out, C);
  and and_15 (and_15_out, not_20_out, B);
  and and_16 (and_16_out, C, not_21_out);
  not not_21 (not_21_out, B);
  and and_17 (and_17_out, C, not_22_out);
  not not_22 (not_22_out, A);
  or or_2 (out_5[6], and_1_out, and_2_out, and_3_out, D);
  or or_3 (out_5[5], not_4_out, and_4_out, and_5_out);
  or or_4 (out_5[3], and_6_out, and_7_out, and_8_out, and_9_out);
  or or_5 (out_5[2], and_10_out, and_11_out);
  or or_6 (out_5[1], and_12_out, and_13_out, and_14_out, D);
  or or_7 (out_5[0], and_15_out, and_16_out, and_17_out, D);

  // Notes on the sheet:
  //   kod wyjsciowy na wyswietlacz
endmodule
