// Logisim project display.circ as structural Verilog: 1 circuit, main circuit main
module main (
  input  [15:0] in_1,
  output [3:0] out_2,
  output [3:0] out_3,
  output [3:0] out_4,
  output [3:0] out_5
);

  // dzielnik_main main_1: pin names not known; wires that end beside it: in_1, out_2, out_3, out_4, out_5
endmodule
