// Logisim project divider.circ as structural Verilog: 1 circuit, main circuit main
module main (
  input  [15:0] in_1,
  output [3:0] out_2,
  output [3:0] out_3,
  output [3:0] out_4,
  output [3:0] out_5
);

  wire [15:0] divider_1_out, divider_1_rem, divider_2_out, divider_2_rem, divider_3_out, divider_3_rem;

  Divider #(.width(16)) divider_1 (.a(in_1), .b(16'h3e8), .out(divider_1_out), .rem(divider_1_rem));  // open: upper
  Bit_Extender #(.in_width(16), .out_width(4)) bit_extender_1 (.in(divider_1_out), .out(out_2));
  Divider #(.width(16)) divider_2 (
    .a(divider_1_rem), .b(16'h64), .out(divider_2_out), .rem(divider_2_rem));  // open: upper
  Bit_Extender #(.in_width(16), .out_width(4)) bit_extender_2 (.in(divider_2_out), .out(out_3));
  Divider #(.width(16)) divider_3 (
    .a(divider_2_rem), .b(16'ha), .out(divider_3_out), .rem(divider_3_rem));  // open: upper
  Bit_Extender #(.in_width(16), .out_width(4)) bit_extender_3 (.in(divider_3_out), .out(out_4));
  Bit_Extender #(.in_width(16), .out_width(4)) bit_extender_4 (.in(divider_3_rem), .out(out_5));
endmodule
