// Logisim project division.circ as structural Verilog: 7 circuits, main circuit main
module main (
  input  in_1,
  input  in_2,
  output [6:0] out_3,
  output [6:0] out_4,
  output [6:0] out_5,
  output [6:0] out_6,
  output [6:0] out_7,
  output [6:0] out_8,
  output [6:0] out_9,
  output [6:0] out_10,
  output [6:0] out_11,
  output [6:0] out_12,
  output [6:0] out_13,
  output [6:0] out_14,
  output [6:0] out_15,
  output [6:0] out_16,
  output [6:0] out_17,
  output [6:0] out_18,
  output [6:0] out_19,
  output [6:0] out_20,
  output [6:0] out_21,
  output [6:0] out_22,
  output [6:0] out_23,
  output [6:0] out_24,
  output [6:0] out_25,
  output [6:0] out_26,
  output [6:0] out_27,
  output [6:0] out_28,
  output [6:0] out_29,
  output [6:0] out_30,
  output [6:0] out_31,
  output [6:0] out_32
);

  wire [10:0] bit_extender_1_out, divider_2_out, divider_2_rem, divider_3_out, divider_3_rem, divider_4_out,
       divider_4_rem;
  wire [31:0] counter_1_q, counter_2_q, divider_1_out, divider_1_rem, multiplier_1_out, register_1_q;

  Counter #(.width(32), .max('hffffffff)) counter_1 (.Q(counter_1_q), .clk(in_1));  // open: load, D, count, carry, clr
  Multiplier #(.width(32)) multiplier_1 (.a(counter_1_q), .b(32'h3e8), .out(multiplier_1_out));  // open: cin, cout
  Counter #(.width(32), .max('hffffffff)) counter_2 (.Q(counter_2_q), .clk(in_2));  // open: load, D, count, carry, clr
  Divider #(.width(32)) divider_1 (
    .a(multiplier_1_out), .b(counter_2_q), .out(divider_1_out), .rem(divider_1_rem));  // open: upper
  _7_Segment_Display u_7_segment_display_1 (
    .g(1'b0), .f(1'b1), .a(1'b1), .b(1'b1), .e(1'b1), .d(1'b1), .c(1'b1), .dp(1'b1));
  Register #(.width(32), .trigger("high")) register_1 (
    .D(divider_1_out), .Q(register_1_q), .clk(1'b1));  // open: en, clr
  Bit_Extender #(.in_width(32), .out_width(11)) bit_extender_1 (.in(register_1_q), .out(bit_extender_1_out));
  Divider #(.width(11)) divider_2 (
    .a(bit_extender_1_out), .b(11'ha), .out(divider_2_out), .rem(divider_2_rem));  // open: upper
  przetwornik przetwornik_1 (
    .in_1(divider_4_out), ._5(out_4), .out_3(out_5), .out_4(out_6), .out_5(out_7), .out_6(out_8));
  przetwornik przetwornik_2 (
    .in_1(divider_4_rem), ._5(out_9), .out_3(out_10), .out_4(out_11), .out_5(out_12), .out_6(out_13));
  przetwornik przetwornik_3 (
    .in_1(divider_3_rem), ._5(out_15), .out_3(out_16), .out_4(out_17), .out_5(out_18), .out_6(out_19));
  przetwornik przetwornik_4 (
    .in_1(divider_2_rem), ._5(out_22), .out_3(out_24), .out_4(out_25), .out_5(out_26), .out_6(out_27));
  Divider #(.width(11)) divider_3 (
    .a(divider_2_out), .b(11'ha), .out(divider_3_out), .rem(divider_3_rem));  // open: upper
  Divider #(.width(11)) divider_4 (
    .a(divider_3_out), .b(11'ha), .out(divider_4_out), .rem(divider_4_rem));  // open: upper

  assign out_3 = {7{1'b0}};
  assign out_14 = {7{1'b0}};
  assign out_20 = {7{1'b0}};
  assign out_21 = {7{1'b0}};
  assign out_23 = 7'b0000001;
  assign out_28 = 7'b1000011;
  assign out_29 = 7'b0000100;
  assign out_30 = 7'b0011000;
  assign out_31 = 7'b0100000;
  assign out_32 = 7'b1000001;

  // Notes on the sheet:
  //   ulamek
  //   jednosci
  //   dziesietne
  //   setki
endmodule

module kolumna1 (
  input  x0,
  input  x1,
  input  x2,
  input  x3,
  output y0,
  output y1,
  output y2,
  output y3,
  output y4,
  output y5,
  output y6
);

  wire and_2_out, and_3_out, and_4_out, and_5_out, and_6_out, and_7_out, and_8_out, and_9_out, and_10_out,
       and_11_out, and_12_out, and_13_out, and_15_out, and_16_out, and_17_out, not_1_out, not_2_out,
       not_3_out, not_4_out, not_5_out, not_6_out, not_7_out, not_8_out, not_9_out, not_10_out, not_11_out,
       not_12_out, not_13_out, not_14_out, not_15_out, not_16_out, not_17_out, not_18_out, not_19_out,
       not_20_out, not_21_out, not_22_out, not_23_out;

  and and_1 (y0, x1, x3);
  not not_1 (not_1_out, x1);
  and and_2 (and_2_out, not_1_out, not_2_out);
  not not_2 (not_2_out, x3);
  and and_3 (and_3_out, x2, x3);
  not not_3 (not_3_out, x1);
  and and_4 (and_4_out, not_3_out, not_4_out);
  not not_4 (not_4_out, x3);
  not not_5 (not_5_out, x1);
  and and_5 (and_5_out, not_5_out, x2);
  not not_6 (not_6_out, x0);
  not not_7 (not_7_out, x1);
  not not_8 (not_8_out, x2);
  not not_9 (not_9_out, x3);
  not not_10 (not_10_out, x2);
  not not_11 (not_11_out, x2);
  and and_6 (and_6_out, not_11_out, not_12_out);
  not not_12 (not_12_out, x3);
  not not_13 (not_13_out, x1);
  and and_7 (and_7_out, not_13_out, x2, x3);
  and and_8 (and_8_out, x1, not_14_out);
  not not_14 (not_14_out, x2);
  and and_9 (and_9_out, x1, not_15_out);
  not not_15 (not_15_out, x3);
  not not_16 (not_16_out, x1);
  and and_10 (and_10_out, not_16_out, not_17_out, not_18_out);
  not not_17 (not_17_out, x2);
  not not_18 (not_18_out, x3);
  not not_19 (not_19_out, x1);
  and and_11 (and_11_out, not_19_out, x2, x3);
  not not_20 (not_20_out, x2);
  and and_12 (and_12_out, x1, not_20_out, x3);
  and and_13 (and_13_out, x1, x2, not_21_out);
  not not_21 (not_21_out, x3);
  not not_22 (not_22_out, x1);
  and and_14 (y6, not_22_out, x2, not_23_out);
  not not_23 (not_23_out, x3);
  or or_1 (y1, and_2_out, and_3_out, x0);
  or or_2 (y2, and_4_out, and_5_out, x0);
  and and_15 (and_15_out, not_6_out, not_7_out, not_8_out, not_9_out);
  and and_16 (and_16_out, x1, not_10_out, x3);
  or or_3 (y3, and_15_out, and_16_out, and_17_out);
  and and_17 (and_17_out, x0, x3);
  or or_4 (y4, and_6_out, and_7_out, and_8_out, and_9_out, x0);
  or or_5 (y5, and_10_out, and_11_out, and_12_out, and_13_out);
endmodule

module kolumna2 (
  input  x0,
  input  x1,
  input  x2,
  input  x3,
  output y0,
  output y1,
  output y2,
  output y3,
  output y4,
  output y5,
  output y6
);

  wire and_2_out, and_3_out, and_4_out, and_5_out, and_7_out, and_8_out, and_9_out, and_10_out, not_1_out,
       not_2_out, not_3_out, not_4_out, not_5_out, not_6_out, not_7_out, not_8_out, not_9_out, not_10_out,
       not_11_out, not_12_out, not_13_out, not_14_out, not_15_out, not_16_out, not_17_out;

  not not_1 (not_1_out, x3);
  and and_1 (y1, x1, not_2_out, not_3_out);
  not not_2 (not_2_out, x2);
  not not_3 (not_3_out, x3);
  not not_4 (not_4_out, x0);
  not not_5 (not_5_out, x2);
  and and_2 (and_2_out, not_4_out, not_5_out, not_6_out);
  not not_6 (not_6_out, x3);
  and and_3 (and_3_out, x1, x3);
  not not_7 (not_7_out, x1);
  and and_4 (and_4_out, not_7_out, x2);
  and and_5 (and_5_out, x1, not_8_out);
  not not_8 (not_8_out, x3);
  not not_9 (not_9_out, x2);
  and and_6 (y4, x1, not_9_out, not_10_out);
  not not_10 (not_10_out, x3);
  and and_7 (and_7_out, x1, not_11_out, not_12_out);
  not not_11 (not_11_out, x2);
  not not_12 (not_12_out, x3);
  and and_8 (and_8_out, x0, x3);
  not not_13 (not_13_out, x0);
  and and_9 (and_9_out, not_13_out, not_14_out);
  not not_14 (not_14_out, x1);
  not not_15 (not_15_out, x0);
  and and_10 (and_10_out, not_15_out, not_16_out);
  not not_16 (not_16_out, x2);
  not not_17 (not_17_out, x3);
  or or_1 (y0, not_1_out, x2, x1, x0);
  or or_2 (y2, and_2_out, and_3_out);
  or or_3 (y3, and_4_out, and_5_out, x0);
  or or_4 (y5, and_7_out, and_8_out);
  or or_5 (y6, and_9_out, and_10_out, not_17_out);
endmodule

module kolumna3 (
  input  x0,
  input  x1,
  input  x2,
  input  x3,
  output y0,
  output y1,
  output y2,
  output y3,
  output y4,
  output y5,
  output y6
);

  wire and_2_out, and_3_out, and_4_out, and_5_out, and_6_out, and_7_out, not_1_out, not_2_out, not_3_out,
       not_4_out, not_5_out, not_6_out, not_7_out, not_8_out, not_9_out, not_10_out, not_11_out, not_12_out,
       not_13_out, not_14_out, not_15_out, not_16_out, not_17_out, not_18_out, not_19_out, not_20_out;

  not not_1 (not_1_out, x1);
  or or_1 (y0, not_1_out, x3, x2);
  not not_2 (not_2_out, x0);
  not not_3 (not_3_out, x1);
  not not_4 (not_4_out, x2);
  not not_5 (not_5_out, x2);
  not not_6 (not_6_out, x3);
  not not_7 (not_7_out, x0);
  not not_8 (not_8_out, x2);
  and and_1 (y2, not_7_out, not_8_out, x3);
  not not_9 (not_9_out, x1);
  or or_2 (y3, not_9_out, x2);
  not not_10 (not_10_out, x0);
  not not_11 (not_11_out, x1);
  not not_12 (not_12_out, x2);
  not not_13 (not_13_out, x2);
  not not_14 (not_14_out, x3);
  not not_15 (not_15_out, x0);
  not not_16 (not_16_out, x1);
  not not_17 (not_17_out, x2);
  not not_18 (not_18_out, x1);
  not not_19 (not_19_out, x2);
  and and_2 (and_2_out, not_19_out, x3);
  and and_3 (and_3_out, x2, not_20_out);
  not not_20 (not_20_out, x3);
  and and_4 (and_4_out, not_2_out, not_3_out, not_4_out, x3);
  or or_3 (y1, and_4_out, and_5_out);
  and and_5 (and_5_out, x1, not_5_out, not_6_out);
  and and_6 (and_6_out, not_10_out, not_11_out, not_12_out, x3);
  or or_4 (y4, and_6_out, and_7_out);
  and and_7 (and_7_out, x1, not_13_out, not_14_out);
  and and_8 (y5, not_15_out, not_16_out, not_17_out, x3);
  or or_5 (y6, not_18_out, and_2_out, and_3_out);
endmodule

module kolumna4 (
  input  x0,
  input  x1,
  input  x2,
  input  x3,
  output y0,
  output y1,
  output y2,
  output y3,
  output y4,
  output y5,
  output y6
);

  wire and_1_out, and_2_out, and_3_out, and_4_out, and_5_out, and_8_out, and_9_out, and_10_out, not_1_out,
       not_2_out, not_3_out, not_4_out, not_5_out, not_6_out, not_7_out, not_8_out, not_9_out, not_10_out,
       not_11_out, not_12_out, not_13_out;

  not not_1 (not_1_out, x1);
  and and_1 (and_1_out, not_1_out, not_2_out);
  not not_2 (not_2_out, x3);
  not not_3 (not_3_out, x1);
  and and_2 (and_2_out, not_3_out, x2);
  and and_3 (and_3_out, x1, x3);
  not not_4 (not_4_out, x1);
  and and_4 (and_4_out, not_4_out, not_5_out, x3);
  not not_5 (not_5_out, x2);
  and and_5 (and_5_out, x1, x2, not_6_out);
  not not_6 (not_6_out, x3);
  and and_6 (y2, x1, not_7_out);
  not not_7 (not_7_out, x2);
  and and_7 (y3, x1, x2, not_8_out);
  not not_8 (not_8_out, x3);
  not not_9 (not_9_out, x1);
  and and_8 (and_8_out, not_9_out, not_10_out);
  not not_10 (not_10_out, x3);
  not not_11 (not_11_out, x2);
  and and_9 (and_9_out, not_11_out, not_12_out);
  not not_12 (not_12_out, x3);
  and and_10 (and_10_out, x1, x2, x3);
  and and_11 (y5, x1, x2, x3);
  not not_13 (not_13_out, x1);
  or or_1 (y6, not_13_out, x3, x2);
  or or_2 (y0, and_1_out, and_2_out, and_3_out);
  or or_3 (y1, and_4_out, and_5_out);
  or or_4 (y4, and_8_out, and_9_out, and_10_out);
endmodule

module kolumna5 (
  input  x0,
  input  x1,
  input  x2,
  input  x3,
  output y0,
  output y1,
  output y2,
  output y3,
  output y4,
  output y5,
  output y6
);

  wire and_2_out, and_3_out, and_4_out, and_5_out, and_6_out, and_7_out, and_8_out, and_9_out, and_10_out,
       and_11_out, and_12_out, and_13_out, and_14_out, and_15_out, not_1_out, not_2_out, not_3_out,
       not_4_out, not_5_out, not_6_out, not_7_out, not_8_out, not_9_out, not_10_out, not_11_out, not_12_out,
       not_13_out, not_14_out, not_15_out, not_16_out, not_17_out, not_18_out, not_19_out, not_20_out,
       not_21_out, not_22_out, not_23_out;

  and and_1 (y0, x1, x3);
  not not_1 (not_1_out, x1);
  and and_2 (and_2_out, not_1_out, not_2_out);
  not not_2 (not_2_out, x3);
  not not_3 (not_3_out, x1);
  and and_3 (and_3_out, not_3_out, x2);
  and and_4 (and_4_out, x1, not_4_out, x3);
  not not_4 (not_4_out, x2);
  not not_5 (not_5_out, x1);
  and and_5 (and_5_out, not_5_out, not_6_out, not_7_out);
  not not_6 (not_6_out, x2);
  not not_7 (not_7_out, x3);
  and and_6 (and_6_out, x1, not_8_out, x3);
  not not_8 (not_8_out, x2);
  and and_7 (and_7_out, x1, x2, not_9_out);
  not not_9 (not_9_out, x3);
  not not_10 (not_10_out, x0);
  and and_8 (and_8_out, not_10_out, not_11_out, not_12_out);
  not not_11 (not_11_out, x2);
  not not_12 (not_12_out, x3);
  and and_9 (and_9_out, x1, not_13_out);
  not not_13 (not_13_out, x3);
  not not_14 (not_14_out, x2);
  and and_10 (and_10_out, not_14_out, not_15_out);
  not not_15 (not_15_out, x3);
  and and_11 (and_11_out, x1, not_16_out);
  not not_16 (not_16_out, x3);
  not not_17 (not_17_out, x1);
  and and_12 (and_12_out, not_17_out, not_18_out);
  not not_18 (not_18_out, x3);
  not not_19 (not_19_out, x1);
  and and_13 (and_13_out, not_19_out, x2);
  and and_14 (and_14_out, x2, not_20_out);
  not not_20 (not_20_out, x3);
  not not_21 (not_21_out, x2);
  and and_15 (and_15_out, x1, not_21_out, x3);
  not not_22 (not_22_out, x1);
  and and_16 (y6, not_22_out, x2, not_23_out);
  not not_23 (not_23_out, x3);
  or or_1 (y1, and_2_out, and_3_out, and_4_out, x0);
  or or_2 (y2, and_5_out, and_6_out, and_7_out, x0);
  or or_3 (y3, and_8_out, and_9_out);
  or or_4 (y4, and_10_out, and_11_out);
  or or_5 (y5, and_12_out, and_13_out, and_14_out, and_15_out);
endmodule

module przetwornik (
  input  [10:0] in_1,
  output [6:0] _5,
  output [6:0] out_3,
  output [6:0] out_4,
  output [6:0] out_5,
  output [6:0] out_6
);

  kolumna5 kolumna5_1 (
    .x0(in_1[3]), .x1(in_1[3]), .x2(in_1[1]), .x3(in_1[0]), .y0(_5[0]), .y1(_5[1]), .y2(_5[2]), .y3(_5[3]),
    .y4(_5[4]), .y5(_5[5]), .y6(_5[6]));
  kolumna4 kolumna4_1 (
    .x0(in_1[3]), .x1(in_1[3]), .x2(in_1[1]), .x3(in_1[0]), .y0(out_3[0]), .y1(out_3[1]), .y2(out_3[2]),
    .y3(out_3[3]), .y4(out_3[4]), .y5(out_3[5]), .y6(out_3[6]));
  kolumna3 kolumna3_1 (
    .x0(in_1[3]), .x1(in_1[3]), .x2(in_1[1]), .x3(in_1[0]), .y0(out_4[0]), .y1(out_4[1]), .y2(out_4[2]),
    .y3(out_4[3]), .y4(out_4[4]), .y5(out_4[5]), .y6(out_4[6]));
  kolumna2 kolumna2_1 (
    .x0(in_1[3]), .x1(in_1[3]), .x2(in_1[1]), .x3(in_1[0]), .y0(out_5[0]), .y1(out_5[1]), .y2(out_5[2]),
    .y3(out_5[3]), .y4(out_5[4]), .y5(out_5[5]), .y6(out_5[6]));
  kolumna1 kolumna1_1 (
    .x0(in_1[3]), .x1(in_1[3]), .x2(in_1[1]), .x3(in_1[0]), .y0(out_6[0]), .y1(out_6[1]), .y2(out_6[2]),
    .y3(out_6[3]), .y4(out_6[4]), .y5(out_6[5]), .y6(out_6[6]));

  assign in_1[2] = in_1[3];

  // Notes on the sheet:
  //   1
endmodule
