// Logisim project division_with_rest.circ as structural Verilog: 1 circuit, main circuit main
module main (
  input  [15:0] liczba_1,
  input  [15:0] liczba_2,
  output [15:0] wynik,
  output [15:0] reszta_z_dzielenia
);

  wire and_1_out, comparator_1_lt, comparator_2_lt, comparator_3_eq, comparator_3_lt, or_1_out;
  wire [15:0] divider_1_out, multiplexer_1_out;

  // Probe on liczba_1
  // Probe on liczba_2
  Comparator #(.width(16)) comparator_1 (.a({16{1'b0}}), .b(liczba_1), .lt(comparator_1_lt));  // open: gt, eq
  Divider #(.width(16)) divider_1 (
    .a(liczba_1), .b(liczba_2), .out(divider_1_out), .rem(reszta_z_dzielenia));  // open: upper
  Comparator #(.width(16)) comparator_2 (.a({16{1'b0}}), .b(liczba_2), .lt(comparator_2_lt));  // open: gt, eq
  // Probe on reszta_z_dzielenia
  and and_1 (and_1_out, comparator_1_lt, comparator_2_lt);
  Comparator #(.width(16)) comparator_3 (
    .a(divider_1_out), .b(16'h270f), .eq(comparator_3_eq), .lt(comparator_3_lt));  // open: gt
  Multiplexer #(.width(16), .enable("false")) multiplexer_1 (
    .in0({16{1'b0}}), .in1(divider_1_out), .out(multiplexer_1_out), .sel(or_1_out));
  or or_1 (or_1_out, comparator_3_eq, comparator_3_lt);
  // Probe on wynik
  Multiplexer #(.width(16), .enable("false")) multiplexer_2 (
    .in0({16{1'b0}}), .in1(multiplexer_1_out), .out(wynik), .sel(and_1_out));
endmodule
