// Logisim project led_show.circ as structural Verilog: 1 circuit, main circuit main
module main (
  input  in_1,
  input  x,
  input  in_3,
  input  in_4,
  input  reset,
  output [24:0] led
);

  wire or_1_out;
  wire [3:0] register_1_q;

  or or_1 (or_1_out, in_1, x, in_3, in_4);
  Register #(.width(4)) register_1 (
    .D({in_1, x, in_3, in_4}), .Q(register_1_q), .clk(or_1_out), .clr(reset));  // open: en
  ROM #(.addrWidth(4), .dataWidth(25)) rom_1 (.addr(register_1_q), .data(led));  // open: sel

  // Notes on the sheet:
  //   contents of rom_1 (hex, n*v repeats v):
  //   0 427c84 421084 0 1151151 0 0 0 425484
endmodule
