// Logisim project main.circ as structural Verilog: 2 circuits, main circuit main
module main (
  input  [4:0] in_1,
  input  [4:0] in_2,
  input  [4:0] in_3,
  input  [4:0] in_4,
  input  [4:0] in_5
);

  wire _0_out, _1_out, _2_out, _3_out, _4_out, _5_out, _6_out, _7_out, _8_out, _9_out, button_2_out,
       button_3_out, button_out, comparator_1_eq, RESET_out, x_out, zegar_klaw_out, zegar_stanu_out;
  wire [2:0] bit_0_stanu_out, stan_q;
  wire [3:0] bit_0_out, register_1_q, transistor_1_out, transistor_2_out;
  wire [6:0] main_2_p2, main_2_p3, main_2_p4, main_2_p5, przetwornik_1_p1;
  wire [15:0] pamiec_1_liczba, pamiec_2_liczba, transistor_3_out;
  wire [24:0] main_1_p6;

  Button button (.out(button_out));
  Button x (.out(x_out));
  Button _7 (.out(_7_out));
  Button _8 (.out(_8_out));
  Button _5 (.out(_5_out));
  Button _4 (.out(_4_out));
  Button _2 (.out(_2_out));
  Button _1 (.out(_1_out));
  or zegar_klaw (zegar_klaw_out, _9_out, _8_out, _7_out, _6_out, _5_out, _4_out, _3_out, _2_out, _1_out, _0_out);
  Button button_2 (.out(button_2_out));
  Button button_3 (.out(button_3_out));
  Button _9 (.out(_9_out));
  Button _6 (.out(_6_out));
  Button _3 (.out(_3_out));
  Button _0 (.out(_0_out));
  Button RESET (.out(RESET_out));
  or bit_3 (bit_0_out[3], _8_out, _9_out);
  buf zegar_stanu (zegar_stanu_out, button_2_out);  // OR_Gate
  // wyswietlanie_main main_1: pin names not known; wires that end beside it: button_2_out, button_3_out, x_out, button_out, RESET_out, main_1_p6
  or bit_2 (bit_0_out[2], _4_out, _5_out, _7_out, _6_out);
  or bit_1 (bit_0_out[1], _2_out, _3_out, _7_out, _6_out);
  buf bit_0_stanu (bit_0_stanu_out[0], button_2_out);  // OR_Gate
  or bit_0 (bit_0_out[0], _1_out, _3_out, _5_out, _7_out, _9_out);
  buf bit_1_stanu (bit_0_stanu_out[1], 1'b0);  // OR_Gate
  DotMatrix #(.matrixrows(5)) dotmatrix_1 (
    .col0(main_1_p6[24:20]), .col1(main_1_p6[19:15]), .col2(main_1_p6[14:10]), .col3(main_1_p6[9:5]),
    .col4(main_1_p6[4:0]));
  buf bit_2_stanu (bit_0_stanu_out[2], 1'b0);  // OR_Gate
  DotMatrix #(.matrixrows(5)) dotmatrix_2 (.col0(in_1), .col1(in_2), .col2(in_3), .col3(in_4), .col4(in_5));
  Register #(.width(3)) stan (.D(bit_0_stanu_out), .Q(stan_q), .clk(zegar_stanu_out), .clr(RESET_out));  // open: en
  // Probe on pamiec_1_liczba
  Transistor #(.\type ("n"), .width(4)) transistor_1 (.in(bit_0_out), .out(transistor_1_out), .gate(comparator_1_eq));
  pamiec pamiec_1 (
    .nowa_cyfra(transistor_1_out), .zegar_klawiatury(zegar_klaw_out), .reset(RESET_out),
    .liczba(pamiec_1_liczba));
  Transistor #(.width(4)) transistor_2 (.in(bit_0_out), .out(transistor_2_out), .gate(comparator_1_eq));
  // Probe on pamiec_2_liczba
  pamiec pamiec_2 (
    .nowa_cyfra(transistor_2_out), .zegar_klawiatury(zegar_klaw_out), .reset(RESET_out),
    .liczba(pamiec_2_liczba));
  Comparator #(.width(3)) comparator_1 (.a(3'b000), .b(stan_q), .eq(comparator_1_eq));  // open: gt, lt
  Transistor #(.\type ("n"), .width(16)) transistor_3 (
    .in(pamiec_1_liczba), .out(transistor_3_out), .gate(comparator_1_eq));
  Transistor #(.width(16)) transistor_4 (.in(pamiec_2_liczba), .out(transistor_3_out), .gate(comparator_1_eq));
  // obsluga_wyswietlacz_main main_2: pin names not known; wires that end beside it: transistor_3_out, main_2_p2, main_2_p3, main_2_p4, main_2_p5
  _7_Segment_Display u_7_segment_display_1 (
    .g(main_2_p2[0]), .f(main_2_p2[1]), .a(main_2_p2[6]), .b(main_2_p2[5]), .e(main_2_p2[2]),
    .d(main_2_p2[3]), .c(main_2_p2[4]));  // open: dp
  _7_Segment_Display u_7_segment_display_2 (
    .g(main_2_p3[0]), .f(main_2_p3[1]), .a(main_2_p3[6]), .b(main_2_p3[5]), .e(main_2_p3[2]),
    .d(main_2_p3[3]), .c(main_2_p3[4]));  // open: dp
  // przetwornik przetwornik_1: pin names not known; wires that end beside it: przetwornik_1_p1
  Register #(.width(4)) register_1 (
    .D(bit_0_out), .Q(register_1_q), .clk(zegar_klaw_out), .clr(RESET_out));  // open: en
  _7_Segment_Display u_7_segment_display_3 (
    .g(main_2_p4[0]), .f(main_2_p4[1]), .a(main_2_p4[6]), .b(main_2_p4[5]), .e(main_2_p4[2]),
    .d(main_2_p4[3]), .c(main_2_p4[4]));  // open: dp
  _7_Segment_Display u_7_segment_display_4 (
    .g(main_2_p5[0]), .f(main_2_p5[1]), .a(main_2_p5[6]), .b(main_2_p5[5]), .e(main_2_p5[2]),
    .d(main_2_p5[3]), .c(main_2_p5[4]));  // open: dp
  _7_Segment_Display u_7_segment_display_5 (
    .g(przetwornik_1_p1[0]), .f(przetwornik_1_p1[1]), .a(przetwornik_1_p1[6]), .b(przetwornik_1_p1[5]),
    .e(przetwornik_1_p1[2]), .d(przetwornik_1_p1[3]), .c(przetwornik_1_p1[4]));  // open: dp

  // Notes on the sheet:
  //   stany układu
  //   0 - wpisanie 1 liczby
  //   1 - działanie + wpisanie 2 liczby 
  //   5 - wypisanie wyniku
  //   podpowiedz jaka liczba jest zapisana
  //   typu n
  //   podpowiedz jaka liczba jest zapisana
  //   typu p
endmodule

module pamiec (
  input  [3:0] nowa_cyfra,
  input  zegar_klawiatury,
  input  reset,
  output [15:0] liczba
);

  wire [15:0] multiplier_1_out;

  Multiplier #(.width(16)) multiplier_1 (
    .a(liczba), .b(16'ha), .out(multiplier_1_out), .cin({{12{1'b0}}, nowa_cyfra}));  // open: cout
  Register #(.width(16), .trigger("falling")) register_1 (
    .D(multiplier_1_out), .Q(liczba), .clk(zegar_klawiatury), .clr(reset));  // open: en
endmodule
