// Logisim project main_file_of_project.circ as structural Verilog: 3 circuits, main circuit main
module main (
);

  wire _0, _1, _2, _3, _4, _5, _6, _7, _8, _9, clear, clock, main_1_p6, reset, save, show, tunnel, tunnel_t,
       tunnel_t_t, tunnel_t_t_t, x;
  wire [2:0] brok;
  wire [3:0] out;
  wire [6:0] dzialania_1_out_18, dzialania_1_out_19, dzialania_1_out_20, dzialania_1_out_21,
       dzialania_1_out_22, dzialania_1_out_23, dzialania_1_out_24, dzialania_1_out_25,
       dzialania_1_wyswietlacz_dol, main_3_p1, main_3_p2, main_3_p4, main_3_p5, znak, znak_out;
  wire [15:0] dzialania_1_reszta, odczyt, or_2_out, wynik;
  wire [24:0] main_4_p6;

  Button u__7 (.out(_7));
  Button u__4 (.out(_4));
  Button u__1 (.out(_1));
  Button u_SHOW (.out(show));
  Button u_SAVE (.out(save));
  Button u_CLEAR (.out(clear));
  Button u__8 (.out(_8));
  Button u__5 (.out(_5));
  Button u__2 (.out(_2));
  Button u__0 (.out(_0));
  Button u__9 (.out(_9));
  Button u__6 (.out(_6));
  Button u__3 (.out(_3));
  Button u_RESET (.out(reset));
  // obsluga_klawiatury_main main_1: pin names not known; wires that end beside it: _0, _1, _2, _3, _4, main_1_p6, _5, _6, _7, brok, _8, _9, out, clock
  or or_1 (main_1_p6, reset, tunnel_t_t, tunnel, tunnel_t, x);
  Button button (.out(tunnel));
  Button button_2 (.out(tunnel_t));
  Button u_x (.out(x));
  Button button_3 (.out(tunnel_t_t));
  Button button_4 (.out(tunnel_t_t_t));
  // ram_pamiec_main main_2: pin names not known; wires that end beside it: show, znak, wynik, save, clear, odczyt, znak_out
  _7_Segment_Display u_7_segment_display_1 (
    .g(znak_out[0]), .f(znak_out[1]), .a(znak_out[6]), .b(znak_out[5]), .e(znak_out[2]), .d(znak_out[3]),
    .c(znak_out[4]));  // open: dp
  _7_Segment_Display u_7_segment_display_2 (
    .g(main_3_p5[0]), .f(main_3_p5[1]), .a(main_3_p5[6]), .b(main_3_p5[5]), .e(main_3_p5[2]),
    .d(main_3_p5[3]), .c(main_3_p5[4]));  // open: dp
  dzialania dzialania_1 (
    .out(out), .clock(clock), .reset_2(reset), .brok(brok), .brok_2(brok), .x(x), .in_9(tunnel_t),
    .in_12(tunnel), .in_10(tunnel_t_t), .in_13(tunnel_t_t_t), .reset_6(reset), .reset_7(reset),
    .reset_8(reset), .reset_4(reset), .reset_3(reset), .reset_5(reset), .reset(reset),
    .wyswietlacz_dol({{5{dzialania_1_wyswietlacz_dol[6]}}, dzialania_1_wyswietlacz_dol[1:0]}),
    .out_22(dzialania_1_out_22), .out_23(dzialania_1_out_23), .out_24(dzialania_1_out_24),
    .out_25(dzialania_1_out_25), .out_18(dzialania_1_out_18), .out_19(dzialania_1_out_19),
    .out_20(dzialania_1_out_20), .out_21(dzialania_1_out_21), .reszta(dzialania_1_reszta), .wynik(wynik),
    .znak(znak));
  assign or_2_out = dzialania_1_reszta | odczyt;  // OR_Gate or_2, 16 bits wide
  // obsluga_wyswietlacz_main main_3: pin names not known; wires that end beside it: main_3_p1, main_3_p2, or_2_out, main_3_p4, main_3_p5
  _7_Segment_Display u_7_segment_display_3 (
    .g(main_3_p4[0]), .f(main_3_p4[1]), .a(main_3_p4[6]), .b(main_3_p4[5]), .e(main_3_p4[2]),
    .d(main_3_p4[3]), .c(main_3_p4[4]));  // open: dp
  _7_Segment_Display u_7_segment_display_4 (
    .g(dzialania_1_out_18[0]), .f(dzialania_1_out_18[1]), .a(dzialania_1_out_18[6]),
    .b(dzialania_1_out_18[5]), .e(dzialania_1_out_18[2]), .d(dzialania_1_out_18[3]), .c(dzialania_1_out_18[4]));  // open: dp
  _7_Segment_Display u_7_segment_display_5 (
    .g(main_3_p2[0]), .f(main_3_p2[1]), .a(main_3_p2[6]), .b(main_3_p2[5]), .e(main_3_p2[2]),
    .d(main_3_p2[3]), .c(main_3_p2[4]));  // open: dp
  _7_Segment_Display u_7_segment_display_6 (
    .g(main_3_p1[0]), .f(main_3_p1[1]), .a(main_3_p1[6]), .b(main_3_p1[5]), .e(main_3_p1[2]),
    .d(main_3_p1[3]), .c(main_3_p1[4]));  // open: dp
  _7_Segment_Display u_7_segment_display_7 (
    .g(dzialania_1_out_19[0]), .f(dzialania_1_out_19[1]), .a(dzialania_1_out_19[6]),
    .b(dzialania_1_out_19[5]), .e(dzialania_1_out_19[2]), .d(dzialania_1_out_19[3]), .c(dzialania_1_out_19[4]));  // open: dp
  _7_Segment_Display u_7_segment_display_8 (
    .g(dzialania_1_wyswietlacz_dol[0]), .f(dzialania_1_wyswietlacz_dol[1]),
    .a(dzialania_1_wyswietlacz_dol[6]), .b(dzialania_1_wyswietlacz_dol[6]),
    .e(dzialania_1_wyswietlacz_dol[6]), .d(dzialania_1_wyswietlacz_dol[6]), .c(dzialania_1_wyswietlacz_dol[6]));  // open: dp
  _7_Segment_Display u_7_segment_display_9 (
    .g(dzialania_1_out_20[0]), .f(dzialania_1_out_20[1]), .a(dzialania_1_out_20[6]),
    .b(dzialania_1_out_20[5]), .e(dzialania_1_out_20[2]), .d(dzialania_1_out_20[3]), .c(dzialania_1_out_20[4]));  // open: dp
  _7_Segment_Display u_7_segment_display_10 (
    .g(dzialania_1_out_22[0]), .f(dzialania_1_out_22[1]), .a(dzialania_1_out_22[6]),
    .b(dzialania_1_out_22[5]), .e(dzialania_1_out_22[2]), .d(dzialania_1_out_22[3]), .c(dzialania_1_out_22[4]));  // open: dp
  _7_Segment_Display u_7_segment_display_11 (
    .g(dzialania_1_out_21[0]), .f(dzialania_1_out_21[1]), .a(dzialania_1_out_21[6]),
    .b(dzialania_1_out_21[5]), .e(dzialania_1_out_21[2]), .d(dzialania_1_out_21[3]), .c(dzialania_1_out_21[4]));  // open: dp
  _7_Segment_Display u_7_segment_display_12 (
    .g(dzialania_1_out_23[0]), .f(dzialania_1_out_23[1]), .a(dzialania_1_out_23[6]),
    .b(dzialania_1_out_23[5]), .e(dzialania_1_out_23[2]), .d(dzialania_1_out_23[3]), .c(dzialania_1_out_23[4]));  // open: dp
  _7_Segment_Display u_7_segment_display_13 (
    .g(dzialania_1_out_24[0]), .f(dzialania_1_out_24[1]), .a(dzialania_1_out_24[6]),
    .b(dzialania_1_out_24[5]), .e(dzialania_1_out_24[2]), .d(dzialania_1_out_24[3]), .c(dzialania_1_out_24[4]));  // open: dp
  DotMatrix #(.matrixrows(5)) dotmatrix_1 (
    .col0(main_4_p6[24:20]), .col1(main_4_p6[19:15]), .col2(main_4_p6[14:10]), .col3(main_4_p6[9:5]),
    .col4(main_4_p6[4:0]));
  // wyswietlanie_main main_4: pin names not known; wires that end beside it: tunnel, tunnel_t, x, tunnel_t_t, reset, main_4_p6
  _7_Segment_Display u_7_segment_display_14 (
    .g(dzialania_1_out_25[0]), .f(dzialania_1_out_25[1]), .a(dzialania_1_out_25[6]),
    .b(dzialania_1_out_25[5]), .e(dzialania_1_out_25[2]), .d(dzialania_1_out_25[3]), .c(dzialania_1_out_25[4]));  // open: dp

  // Notes on the sheet:
  //   STANY UKŁADU
  //   STAN 0: WPISANIE 1 LICZBY
  //   STAN 1: WPISANIE 2 LICZBY, OPCJA DODAWANIA
  //   STAN 2: WPISANIE 2 LICZBY, OPCJA MNOŻENIA
  //   STAN 3: WPISANIE 2 LICZBY, OPCJA ODEJMOWANIA
  //   STAN 4: WPISANIE 2 LICZBY, OPCJA DZIELENIA
  //   STAN 5: WYPISANIE WYNIKU, OPCJA RÓWNA SIĘ
  //   RESZTA Z DZIELENIA LUB ODCZYT
endmodule

module pamiec (
  input  [3:0] nowa_cyfra,
  input  zegar_klawiatury,
  input  reset,
  input  [2:0] brok,
  output [15:0] liczba
);

  wire and_1_out, clock_1_out, comparator_1_eq, comparator_2_eq, comparator_3_eq, comparator_4_eq,
       comparator_4_lt, multiplexer_1_out, multiplexer_2_out, multiplexer_3_out, nor_1_out;
  wire [7:0] counter_1_q, counter_2_q, counter_3_q;
  wire [15:0] multiplier_1_out;

  Clock clock_1 (.out(clock_1_out));
  Counter counter_1 (.Q(counter_1_q), .clk(multiplexer_1_out), .clr(comparator_3_eq));  // open: load, D, count, carry
  Multiplexer #(.enable("false")) multiplexer_1 (
    .in0(1'b0), .in1(clock_1_out), .out(multiplexer_1_out), .sel(zegar_klawiatury));
  Counter counter_2 (.Q(counter_2_q), .clk(and_1_out), .clr(comparator_1_eq));  // open: load, D, count, carry
  and and_1 (and_1_out, zegar_klawiatury, comparator_2_eq);
  Counter #(.trigger("falling")) counter_3 (
    .Q(counter_3_q), .clk(zegar_klawiatury), .clr(zegar_klawiatury));  // open: load, D, count, carry
  Comparator #(.mode("unsigned")) comparator_1 (.a(counter_3_q), .b(8'h1), .eq(comparator_1_eq));  // open: gt, lt
  Multiplexer #(.enable("false")) multiplexer_2 (
    .in0(1'b0), .in1(zegar_klawiatury), .out(multiplexer_2_out), .sel(comparator_2_eq));
  Comparator #(.mode("unsigned")) comparator_2 (.a(counter_1_q), .b(8'h3), .eq(comparator_2_eq));  // open: gt, lt
  Comparator #(.mode("unsigned")) comparator_3 (.a(counter_2_q), .b(8'h1), .eq(comparator_3_eq));  // open: gt, lt
  Multiplier #(.width(16)) multiplier_1 (
    .a(liczba), .b(16'ha), .out(multiplier_1_out), .cin({{12{1'b0}}, nowa_cyfra}));  // open: cout
  Multiplexer #(.enable("false")) multiplexer_3 (
    .in0(multiplexer_2_out), .in1(1'b0), .out(multiplexer_3_out), .sel(nor_1_out));
  Comparator #(.width(3), .mode("unsigned")) comparator_4 (
    .a(brok), .b(3'b100), .eq(comparator_4_eq), .lt(comparator_4_lt));  // open: gt
  nor nor_1 (nor_1_out, comparator_4_eq, comparator_4_lt);
  Register #(.width(16), .trigger("falling")) register_1 (
    .D(multiplier_1_out), .Q(liczba), .clk(multiplexer_3_out), .clr(reset));  // open: en

  // Notes on the sheet:
  //   Input delay
  //   Only one click
endmodule

module dzialania (
  input  reset,
  input  [3:0] out,
  input  clock,
  input  reset_2,
  input  [2:0] brok,
  input  reset_3,
  input  [2:0] brok_2,
  input  x,
  input  in_9,
  input  in_10,
  input  reset_4,
  input  in_12,
  input  in_13,
  input  reset_5,
  input  reset_6,
  input  reset_7,
  input  reset_8,
  output [6:0] out_18,
  output [6:0] out_19,
  output [6:0] out_20,
  output [6:0] out_21,
  output [6:0] out_22,
  output [6:0] out_23,
  output [6:0] out_24,
  output [6:0] out_25,
  output [15:0] wynik,
  output [6:0] wyswietlacz_dol,
  output [6:0] znak,
  output [15:0] reszta
);

  wire and_1_out, and_2_out, comparator_1_eq, counter_1_q, counter_2_q, counter_3_q, counter_4_q, main_1_p7,
       main_1_p8, main_1_p9, main_1_p10, main_1_p11, main_1_p12, main_6_p3, nand_1_out, nand_2_out,
       nand_3_out, nand_4_out;
  wire [3:0] transistor_1_out, transistor_2_out;
  wire [15:0] main_2_p3, main_3_p3, main_4_p4, main_4_p5, main_6_p4, multiplexer_1_out, multiplexer_2_out,
       multiplexer_4_out, multiplexer_5_out, multiplexer_6_out, multiplexer_7_out, multiplexer_8_out,
       multiplexer_9_out, pamiec_1_liczba, pamiec_2_liczba, transistor_3_out, transistor_5_out;

  // Probe on out
  // Probe on pamiec_1_liczba
  Transistor #(.\type ("n"), .width(4)) transistor_1 (.in(out), .out(transistor_1_out), .gate(main_1_p7));
  pamiec pamiec_1 (
    .nowa_cyfra(transistor_1_out), .zegar_klawiatury(clock), .reset(reset_2), .brok(brok),
    .liczba(pamiec_1_liczba));
  Transistor #(.width(4)) transistor_2 (.in(out), .out(transistor_2_out), .gate(main_1_p7));
  // Probe on pamiec_2_liczba
  pamiec pamiec_2 (
    .nowa_cyfra(transistor_2_out), .zegar_klawiatury(clock), .reset(reset_2), .brok(brok_2),
    .liczba(pamiec_2_liczba));
  // stan_klawisze_wyjscie_main main_1: pin names not known; wires that end beside it: in_12, in_9, x, in_10, in_13, reset_6, main_1_p7, main_1_p8, main_1_p9, main_1_p10, main_1_p11, main_1_p12
  Transistor #(.\type ("n"), .width(16)) transistor_3 (.in(pamiec_1_liczba), .out(transistor_3_out), .gate(main_1_p7));
  and and_1 (and_1_out, counter_3_q, main_1_p12);
  Transistor #(.width(16)) transistor_4 (.in(pamiec_2_liczba), .out(transistor_3_out), .gate(main_1_p7));
  // dodawanie_main main_2: pin names not known; wires that end beside it: pamiec_1_liczba, pamiec_2_liczba, main_2_p3
  Multiplexer #(.width(16), .enable("false")) multiplexer_1 (
    .in0({16{1'b0}}), .in1(main_3_p3), .out(multiplexer_1_out), .sel(nand_1_out));
  // mnozenie_main main_3: pin names not known; wires that end beside it: pamiec_1_liczba, pamiec_2_liczba, main_3_p3
  nand nand_1 (nand_1_out, main_1_p9, main_1_p12);
  // dzielenie_z_reszta_main main_4: pin names not known; wires that end beside it: reset_7, pamiec_1_liczba, pamiec_2_liczba, main_4_p4, main_4_p5
  Comparator #(.width(1)) comparator_1 (.a(1'b1), .b(and_1_out), .eq(comparator_1_eq));  // open: gt, lt
  // obsluga_wyswietlacz_main main_5: pin names not known; wires that end beside it: transistor_3_out, out_18, out_19, out_20, out_21
  Multiplexer #(.width(16), .enable("false")) multiplexer_2 (
    .in0({16{1'b0}}), .in1(main_2_p3), .out(multiplexer_2_out), .sel(nand_2_out));
  nand nand_2 (nand_2_out, main_1_p8, main_1_p12);
  // odejmowanie_main main_6: pin names not known; wires that end beside it: pamiec_1_liczba, pamiec_2_liczba, main_6_p3, main_6_p4
  Multiplexer #(.width(16), .enable("false")) multiplexer_3 (
    .in0({16{1'b0}}), .in1(main_4_p5), .out(reszta), .sel(comparator_1_eq));
  Multiplexer #(.width(16), .enable("false")) multiplexer_4 (
    .in0({16{1'b0}}), .in1(multiplexer_2_out), .out(multiplexer_4_out), .sel(counter_1_q));
  Counter #(.width(1), .max('h1)) counter_1 (
    .D(main_1_p8), .Q(counter_1_q), .clk(main_1_p8), .clr(reset_3));  // open: load, count, carry
  assign wynik = multiplexer_4_out | multiplexer_5_out | multiplexer_9_out | multiplexer_7_out;  // OR_Gate or_1, 16 bits wide
  Multiplexer #(.width(16), .enable("false")) multiplexer_5 (
    .in0({16{1'b0}}), .in1(multiplexer_1_out), .out(multiplexer_5_out), .sel(counter_2_q));
  Counter #(.width(1), .max('h1)) counter_2 (
    .D(main_1_p9), .Q(counter_2_q), .clk(main_1_p9), .clr(reset_4));  // open: load, count, carry
  Multiplexer #(.width(16), .enable("false")) multiplexer_6 (
    .in0({16{1'b0}}), .in1(main_4_p4), .out(multiplexer_6_out), .sel(nand_3_out));
  nand nand_3 (nand_3_out, main_1_p11, main_1_p12);
  Transistor #(.\type ("n"), .width(16)) transistor_5 (.in(wynik), .out(transistor_5_out), .gate(main_1_p12));
  Pull_Resistor pull_resistor_1 (.node(transistor_5_out));
  and and_2 (and_2_out, main_6_p3, counter_4_q);
  Counter #(.width(1), .max('h1)) counter_3 (
    .D(main_1_p11), .Q(counter_3_q), .clk(main_1_p11), .clr(reset_8));  // open: load, count, carry
  // obsluga_wyswietlacz_main main_7: pin names not known; wires that end beside it: transistor_5_out, out_22, out_23, out_24, out_25
  Multiplexer #(.width(16), .enable("false")) multiplexer_7 (
    .in0({16{1'b0}}), .in1(multiplexer_6_out), .out(multiplexer_7_out), .sel(counter_3_q));
  // minus_wyswietl_main main_8: pin names not known; wires that end beside it: and_2_out, main_1_p12, wyswietlacz_dol, reset
  Multiplexer #(.width(16), .enable("false")) multiplexer_8 (
    .in0({16{1'b0}}), .in1(main_6_p4), .out(multiplexer_8_out), .sel(nand_4_out));
  nand nand_4 (nand_4_out, main_1_p10, main_1_p12);
  Multiplexer #(.width(16), .enable("false")) multiplexer_9 (
    .in0({16{1'b0}}), .in1(multiplexer_8_out), .out(multiplexer_9_out), .sel(counter_4_q));
  Counter #(.width(1), .max('h1)) counter_4 (
    .D(main_1_p10), .Q(counter_4_q), .clk(main_1_p10), .clr(reset_5));  // open: load, count, carry

  assign znak = wyswietlacz_dol;

  // Notes on the sheet:
  //   podpowiedz jaka liczba jest zapisana
  //   podpowiedz jaka liczba jest zapisana
  //   typu p
endmodule
