// Logisim project memory.circ as structural Verilog: 1 circuit, main circuit main
module main (
  input  [3:0] nowa_cyfra,
  input  zegar_klawiatury,
  input  reset,
  input  [2:0] brok,
  output [15:0] liczba
);

  wire and_1_out, clock_1_out, comparator_1_eq, comparator_2_eq, comparator_3_eq, comparator_4_eq,
       comparator_4_lt, multiplexer_1_out, multiplexer_2_out, multiplexer_3_out, nor_1_out;
  wire [7:0] counter_1_q, counter_2_q, counter_3_q;
  wire [15:0] multiplier_1_out;

  Clock clock_1 (.out(clock_1_out));
  Counter counter_1 (.Q(counter_1_q), .clk(multiplexer_1_out), .clr(comparator_3_eq));  // open: load, D, count, carry
  Multiplexer #(.enable("false")) multiplexer_1 (
    .in0(1'b0), .in1(clock_1_out), .out(multiplexer_1_out), .sel(zegar_klawiatury));
  Counter counter_2 (.Q(counter_2_q), .clk(and_1_out), .clr(comparator_1_eq));  // open: load, D, count, carry
  and and_1 (and_1_out, zegar_klawiatury, comparator_2_eq);
  Counter #(.trigger("falling")) counter_3 (
    .Q(counter_3_q), .clk(zegar_klawiatury), .clr(zegar_klawiatury));  // open: load, D, count, carry
  Comparator #(.mode("unsigned")) comparator_1 (.a(counter_3_q), .b(8'h1), .eq(comparator_1_eq));  // open: gt, lt
  Multiplexer #(.enable("false")) multiplexer_2 (
    .in0(1'b0), .in1(zegar_klawiatury), .out(multiplexer_2_out), .sel(comparator_2_eq));
  Comparator #(.mode("unsigned")) comparator_2 (.a(counter_1_q), .b(8'h3), .eq(comparator_2_eq));  // open: gt, lt
  Comparator #(.mode("unsigned")) comparator_3 (.a(counter_2_q), .b(8'h1), .eq(comparator_3_eq));  // open: gt, lt
  Multiplier #(.width(16)) multiplier_1 (
    .a(liczba), .b(16'ha), .out(multiplier_1_out), .cin({{12{1'b0}}, nowa_cyfra}));  // open: cout
  Multiplexer #(.enable("false")) multiplexer_3 (
    .in0(multiplexer_2_out), .in1(1'b0), .out(multiplexer_3_out), .sel(nor_1_out));
  Comparator #(.width(3), .mode("unsigned")) comparator_4 (
    .a(brok), .b(3'b100), .eq(comparator_4_eq), .lt(comparator_4_lt));  // open: gt
  nor nor_1 (nor_1_out, comparator_4_eq, comparator_4_lt);
  Register #(.width(16), .trigger("falling")) register_1 (
    .D(multiplier_1_out), .Q(liczba), .clk(multiplexer_3_out), .clr(reset));  // open: en

  // Notes on the sheet:
  //   Input delay
  //   Only one click
endmodule
