// Logisim project multiplication.circ as structural Verilog: 1 circuit, main circuit main
module main (
  input  [15:0] in_1,
  input  [15:0] in_2,
  output [15:0] out_3
);

  wire comparator_1_eq, comparator_1_lt, or_1_out;
  wire [15:0] multiplier_1_out;

  Multiplier #(.width(16)) multiplier_1 (.a(in_1), .b(in_2), .out(multiplier_1_out));  // open: cin, cout
  Comparator #(.width(16), .mode("unsigned")) comparator_1 (
    .a(multiplier_1_out), .b(16'h270f), .eq(comparator_1_eq), .lt(comparator_1_lt));  // open: gt
  // Probe on out_3
  Multiplexer #(.width(16), .enable("false")) multiplexer_1 (
    .in0({16{1'b0}}), .in1(multiplier_1_out), .out(out_3), .sel(or_1_out));
  or or_1 (or_1_out, comparator_1_eq, comparator_1_lt);
endmodule
