// Logisim project operation_display.circ as structural Verilog: 1 circuit, main circuit main
module main (
  input  [15:0] wejscie,
  output [6:0] out_2,
  output [6:0] out_3,
  output [6:0] out_4,
  output [6:0] out_5
);

  wire [3:0] main_1_p2, main_1_p3, main_1_p4, main_1_p5;

  // dzielnik_main main_1: pin names not known; wires that end beside it: wejscie, main_1_p2, main_1_p3, main_1_p4, main_1_p5
  // przetwornik przetwornik_1: pin names not known; wires that end beside it: out_2
  // przetwornik przetwornik_2: pin names not known; wires that end beside it: out_3
  // przetwornik przetwornik_3: pin names not known; wires that end beside it: out_4
  // przetwornik przetwornik_4: pin names not known; wires that end beside it: out_5

  // Notes on the sheet:
  //   dzielnik
  //   tysiac
  //   setki
  //   dziesiatki
  //   jednosci
endmodule
