// Logisim project operation_keys.circ as structural Verilog: 1 circuit, main circuit main
module main (
  input  _7,
  input  _8,
  input  _9,
  input  _4,
  input  _5,
  input  _6,
  input  _0,
  input  _1,
  input  _2,
  input  _3,
  input  reset,
  output [3:0] \Wartość_wyjściowa_z_klawiszy ,
  output Zegar_klawiatury,
  output [2:0] blokada
);

  wire clock_1_out, comparator_1_lt, multiplexer_1_out, multiplexer_2_out;
  wire [3:0] bit_0_out;

  or zegar_klaw (Zegar_klawiatury, _9, _8, _7, _6, _5, _4, _3, _2, _1, _0);
  or bit_3 (bit_0_out[3], _8, _9);
  or bit_2 (bit_0_out[2], _4, _5, _6, _7);
  or bit_1 (bit_0_out[1], _2, _3, _6, _7);
  or bit_0 (bit_0_out[0], _1, _3, _5, _7, _9);
  Multiplexer #(.enable("false")) multiplexer_1 (
    .in0(1'b0), .in1(Zegar_klawiatury), .out(multiplexer_1_out), .sel(comparator_1_lt));
  Counter #(.width(3), .max('h7)) counter_1 (
    .Q(blokada), .clk(multiplexer_1_out), .clr(reset));  // open: load, D, count, carry
  Clock clock_1 (.out(clock_1_out));
  Comparator #(.width(3), .mode("unsigned")) comparator_1 (
    .a(blokada), .b(3'b101), .lt(comparator_1_lt));  // open: gt, eq
  Register #(.width(4)) register_1 (
    .D(bit_0_out), .Q(\Wartość_wyjściowa_z_klawiszy ), .clk(multiplexer_2_out), .clr(reset));  // open: en
  Multiplexer #(.enable("false")) multiplexer_2 (
    .in0(1'b0), .in1(clock_1_out), .out(multiplexer_2_out), .sel(comparator_1_lt));
endmodule
