// Logisim project operation_memory.circ as structural Verilog: 1 circuit, main circuit main
module main (
  input  [3:0] out,
  input  clock,
  input  reset,
  input  [2:0] brok,
  input  wyjscie_z_bloku_stanu,
  output [15:0] pamiec_2,
  output [15:0] pamiec_1
);

  wire [3:0] transistor_1_out, transistor_2_out;
  wire [15:0] pamiec_1_liczba, pamiec_2_liczba;

  Transistor #(.\type ("n"), .width(4)) transistor_1 (.in(out), .out(transistor_1_out), .gate(wyjscie_z_bloku_stanu));
  pamiec u_pamiec_1 (
    .nowa_cyfra(transistor_1_out), .zegar_klawiatury(clock), .reset(reset), .brok(brok),
    .liczba(pamiec_1_liczba));
  Transistor #(.width(4)) transistor_2 (.in(out), .out(transistor_2_out), .gate(wyjscie_z_bloku_stanu));
  // Probe on pamiec_1_liczba
  pamiec u_pamiec_2 (
    .nowa_cyfra(transistor_2_out), .zegar_klawiatury(clock), .reset(reset), .brok(brok),
    .liczba(pamiec_2_liczba));
  // Probe on pamiec_2_liczba
  Transistor #(.width(16)) transistor_3 (.in(pamiec_1_liczba), .out(pamiec_2), .gate(wyjscie_z_bloku_stanu));
  Pull_Resistor pull_resistor_1 (.node(pamiec_2));
  Pull_Resistor pull_resistor_2 (.node(pamiec_1));
  Transistor #(.width(16)) transistor_4 (.in(pamiec_2_liczba), .out(pamiec_1), .gate(wyjscie_z_bloku_stanu));
endmodule
