// Logisim project ram_memory.circ as structural Verilog: 1 circuit, main circuit main
module main (
  input  show,
  input  [15:0] in_2,
  input  [6:0] in_3,
  input  save,
  input  in_5,
  output [6:0] znak,
  output [15:0] out_7
);

  wire and_1_out, and_2_out, clock_1_out, counter_1_q, counter_2_q, not_1_out, not_2_out, not_3_out;
  wire [6:0] controlled_buffer_2_out;
  wire [15:0] controlled_buffer_1_out;

  // Probe on {8{1'b1}}
  Clock clock_1 (.out(clock_1_out));
  // Probe on in_2
  assign controlled_buffer_1_out = save ? in_2 : 16'bz;  // Controlled_Buffer controlled_buffer_1
  and and_1 (and_1_out, show, not_1_out);
  Counter #(.width(1), .max('h1)) counter_1 (
    .D(and_1_out), .Q(counter_1_q), .clk(show));  // open: load, count, carry, clr
  not not_1 (not_1_out, save);
  // Probe on out_7
  Multiplexer #(.width(16), .enable("false")) multiplexer_1 (
    .in0({16{1'b0}}), .in1(controlled_buffer_1_out), .out(out_7), .sel(counter_1_q));
  // Probe on controlled_buffer_1_out
  RAM #(.dataWidth(16)) ram_1 (
    .addr({8{1'b1}}), .data(controlled_buffer_1_out), .clk(clock_1_out), .ld(not_1_out), .clr(in_5));  // open: sel
  not not_2 (not_2_out, not_3_out);
  assign controlled_buffer_2_out = save ? in_3 : 7'bz;  // Controlled_Buffer controlled_buffer_2
  and and_2 (and_2_out, show, not_2_out);
  Counter #(.width(1), .max('h1)) counter_2 (
    .D(and_2_out), .Q(counter_2_q), .clk(show));  // open: load, count, carry, clr
  RAM #(.addrWidth(7), .dataWidth(7)) ram_2 (
    .addr({7{1'b1}}), .data(controlled_buffer_2_out), .clk(clock_1_out), .ld(not_3_out), .clr(in_5));  // open: sel
  not not_3 (not_3_out, save);
  Multiplexer #(.width(7), .enable("false")) multiplexer_2 (
    .in0({7{1'b0}}), .in1(controlled_buffer_2_out), .out(znak), .sel(counter_2_q));
endmodule
