// Logisim project selector.circ as structural Verilog: 1 circuit, main circuit main
module main (
  input  [2:0] in_1,
  output out_2,
  output out_3,
  output out_4,
  output out_5,
  output out_6,
  output out_7
);

  Comparator #(.width(3)) comparator_1 (.a(3'b000), .b(in_1), .eq(out_2));  // open: gt, lt
  Comparator #(.width(3)) comparator_2 (.a(3'b001), .b(in_1), .eq(out_3));  // open: gt, lt
  Comparator #(.width(3)) comparator_3 (.a(3'b010), .b(in_1), .eq(out_4));  // open: gt, lt
  Comparator #(.width(3)) comparator_4 (.a(3'b011), .b(in_1), .eq(out_5));  // open: gt, lt
  Comparator #(.width(3)) comparator_5 (.a(3'b100), .b(in_1), .eq(out_6));  // open: gt, lt
  Comparator #(.width(3)) comparator_6 (.a(3'b101), .b(in_1), .eq(out_7));  // open: gt, lt
endmodule
