// Logisim project show_minus.circ as structural Verilog: 1 circuit, main circuit main
module main (
  input  \wyjście_z_odejmowania ,
  input  stan_przycisku_rownosci,
  input  reset,
  output [6:0] wyswietlacz
);

  wire and_1_out;
  wire [1:0] register_1_q;

  and and_1 (and_1_out, \wyjście_z_odejmowania , stan_przycisku_rownosci);
  Register #(.width(2)) register_1 (
    .D({1'b0, \wyjście_z_odejmowania }), .Q(register_1_q), .clk(and_1_out), .clr(reset));  // open: en
  ROM #(.addrWidth(2), .dataWidth(7)) rom_1 (.addr(register_1_q), .data(wyswietlacz));  // open: sel

  // Notes on the sheet:
  //   contents of rom_1 (hex, n*v repeats v):
  //   0 1
endmodule
