// Logisim project state_exit_keys.circ as structural Verilog: 1 circuit, main circuit main
module main (
  input  in_1,
  input  in_2,
  input  x,
  input  in_4,
  input  in_5,
  input  reset,
  output _0,
  output _1,
  output _2,
  output _3,
  output _4,
  output _5
);

  wire zegar_stanu_out;
  wire [2:0] bit_0_stanu_out, stan_q;

  or zegar_stanu (zegar_stanu_out, in_1, in_2, x, in_4, in_5);
  or bit_0_stanu (bit_0_stanu_out[0], in_1, in_2, in_5);
  or bit_1_stanu (bit_0_stanu_out[1], in_2, x);
  or bit_2_stanu (bit_0_stanu_out[2], in_4, in_5);
  Register #(.width(3)) stan (.D(bit_0_stanu_out), .Q(stan_q), .clk(zegar_stanu_out), .clr(reset));  // open: en
  // wybierak_main main_1: pin names not known; wires that end beside it: stan_q, _0, _1, _2, _3, _4, _5
endmodule
