// Logisim project substraction.circ as structural Verilog: 1 circuit, main circuit main
module main (
  input  [15:0] in_1,
  input  [15:0] in_2,
  output out_3,
  output [15:0] out_4
);

  wire not_2_out;
  wire [15:0] adder_1_out, not_1_out, subtractor_1_out;

  // Probe on in_1
  // Probe on in_2
  Subtractor #(.width(16)) subtractor_1 (.a(in_1), .b(in_2), .out(subtractor_1_out));  // open: bin, bout
  Comparator #(.width(16)) comparator_1 (.a(subtractor_1_out), .b({16{1'b0}}), .lt(out_3));  // open: gt, eq
  assign not_1_out = ~subtractor_1_out;  // NOT_Gate not_1, 16 bits wide
  assign out_4 = not_2_out ? subtractor_1_out : 16'bz;  // Controlled_Buffer controlled_buffer_1
  not not_2 (not_2_out, out_3);
  Adder #(.width(16)) adder_1 (.a(not_1_out), .b(16'h1), .out(adder_1_out));  // open: cin, cout
  // Probe on out_4
  assign out_4 = out_3 ? adder_1_out : 16'bz;  // Controlled_Buffer controlled_buffer_2
endmodule
