// Logisim project u2_sub.circ as structural Verilog: 1 circuit, main circuit main
module main (
  input  [5:0] in_1,
  input  [5:0] in_2,
  output Znak__minus,
  output [5:0] out_4
);

  wire not_2_out;
  wire [5:0] adder_1_out, not_1_out, subtractor_1_out;

  Subtractor #(.width(6)) subtractor_1 (.a(in_1), .b(in_2), .out(subtractor_1_out));  // open: bin, bout
  Comparator #(.width(6)) comparator_1 (.a(subtractor_1_out), .b({6{1'b0}}), .lt(Znak__minus));  // open: gt, eq
  assign not_1_out = ~subtractor_1_out;  // NOT_Gate not_1, 6 bits wide
  assign out_4 = not_2_out ? subtractor_1_out : 6'bz;  // Controlled_Buffer controlled_buffer_1
  not not_2 (not_2_out, Znak__minus);
  Adder #(.width(6)) adder_1 (.a(not_1_out), .b(6'b000001), .out(adder_1_out));  // open: cin, cout
  assign out_4 = Znak__minus ? adder_1_out : 6'bz;  // Controlled_Buffer controlled_buffer_2

  // Notes on the sheet:
  //   Kod U2
endmodule
